# Fritzing sketch Transmitter (saved by Fritzing 0.9.3b)
breadboards: 1

parts:
  Part1 = FTDI Basic Programmer
  Part2 = Arduino Pro Mini (3.3V)
  3_3_V_regulator1 = Voltage Regulator LM1117 [package=sot223]
  Part3 = NRF24L01+ Breakout Board
  3_3_uF1 = Capacitor Polarized [package=nippon_f80]
  BAT1 = BC9VPC [package=bc9vpc]
  S1 = Square Pushbutton
  Use_int_pull-up_resistors = Square Pushbutton
  S2 = Square Pushbutton
  Use_int_pull-up_resistors1 = Square Pushbutton

nets:
  N1: Part1.RXI, Part2.TXO
  N2: Part1.TXO, Part2.RXI
  N3: Part1.GND, BAT1.V-, S1.leg1, Use_int_pull-up_resistors.leg1, S2.leg1, Use_int_pull-up_resistors1.leg1
  N4: Part2.D6, S1.leg0
  N5: Part2.D4, Use_int_pull-up_resistors.leg0
  N6: Part2.D3, S2.leg0
  N7: Part2.D2, Use_int_pull-up_resistors1.leg0
  N8: 3_3_V_regulator1.ADJ, Part3.GND, 3_3_uF1.-
  N9: 3_3_V_regulator1.OUT, Part3.VCC
  N10: 3_3_V_regulator1.IN, BAT1.V+
